# Fritzing sketch Prototype final (saved by Fritzing 0.9.3b)
breadboards: 1

parts:
  Composant1 = Arduino Uno (Rev3)
  L1 = Inductor [current=0pA inductance=10mH package="400 mil [THT]"]
  R2 = Resistor [tolerance=±5% resistance=1M package=THT]
  R1 = Resistor [tolerance=±5% resistance=100 package=THT]
  C1 = Tantalum Capacitor [capacitance=1μF package="100 mil [THT, tantalum]"]
  R3 = Resistor [tolerance=±5% resistance=3.6k package=THT]
  C2 = Ceramic Capacitor [capacitance=10nF package="100 mil [THT, multilayer]"]
  C1_2 = Ceramic Capacitor [capacitance=0.1nF package="100 mil [THT, multilayer]"]
  D1 = Rectifier Diode [part_number=1N4001 package="300 mil [THT]"]

nets:
  N1: Composant1.A0, R2.Pin_0, C1_2.1, D1.cathode
  N2: Composant1.D9_PWM, R1.Pin_0
  GND: Composant1.GND, R2.Pin_1, R3.Pin_1, C1_2.0
  N3: L1.pin_0, C2.0, D1.anode
  N4: L1.pin_1, R1.Pin_1, R3.Pin_0
  N5: C1.-, C2.1

// code stored in the sketch: Arduino_sensing.ino
//****************************************************************************************
// Illutron take on Disney style capacitive touch sensor using only passives and Arduino
// Dzl 2012
//****************************************************************************************


//                              10n
// PIN 9 --[10k]-+-----10mH---+--||-- OBJECT
//               |            |
//              3.3k          |
//               |            V 1N4148 diode
//              GND           |
//                            |
//Analog 0 ---+------+--------+
//            |      |
//          100pf   1MOmhm
//            |      |
//           GND    GND



#define SET(x,y) (x |=(1<<y))				//-Bit set/clear macros
#define CLR(x,y) (x &= (~(1<<y)))       		// |
#define CHK(x,y) (x & (1<<y))           		// |
#define TOG(x,y) (x^=(1<<y))            		//-+



#define N 160  //How many frequencies

float results[N];            //-Filtered result buffer
float freq[N];            //-Filtered result buffer
int sizeOfArray = N;

 
   
   

void setup()
{
  
  
  TCCR1A=0b10000010;        //-Set up frequency generator
  TCCR1B=0b00011001;        //-+
  ICR1=110;
  OCR1A=55;

  pinMode(9,OUTPUT);        //-Signal generator pin
  pinMode(8,OUTPUT);        //-Sync (test) pin

  Serial.begin(115200);

  for(int i=0;i<N;i++)      //-Preset results
    results[i]=0;         //-+
}

void loop()
{
  unsigned int d;

  int counter = 0;
  for(unsigned int d=0;d<N;d++)
  {
    int v=analogRead(0);    //-Read response signal
    CLR(TCCR1B,0);          //-Stop generator
    TCNT1=0;                //-Reload new frequency
    ICR1=d;                 // |
    OCR1A=d/2;              //-+
    SET(TCCR1B,0);          //-Restart generator

    results[d]=results[d]*0.5+(float)(v)*0.5; //Filter results
    Serial.println(TCCR1B);
    
 //   plot(v,0);              //-Display
 //   plot(results[d],1);
  // delayMicroseconds(1);
  }
  delay(10000);


    //PlottArray(1,freq,results); 
 

  TOG(PORTB,0);            //-Toggle pin 8 after each sweep (good for scope)
}

// code stored in the sketch: PWM_Freq4.ino
//****************************************************************************************
// PWM Square Wave Generator
// VLO 2013-2014
//****************************************************************************************


const int outPin = 9; // output pin
const float maxFreq = 16000000; //max freq supported by Arduino (16MHz)

void setup()
{

  Serial.begin(115200); //for sending A0 pin values
  
  pinMode(outPin,OUTPUT);        //Signal generator pin
  
  setFrequency(1000000); //generate a square wave (in this case at 1000Hz)
  
  //for test
  //Serial.println();
  //Serial.println(ICR1);
  //Serial.println(TCCR1B);
}

void loop()
{


  int val = analogRead(0);                                              
  Serial.write( 0xff );                                                         
  Serial.write( (val >> 8) & 0xff );                                            
  Serial.write( val & 0xff );
 
}

//set frequency (Hz)
//min frequency: 0.24 Hz
//max frequency: 8MHz
void setFrequency(float frequency)
{
 
  if(frequency >=0.24 || frequency <=8000000)
  {
    
    TCCR1A=0b10000010;        // Set up frequency generator, mode 14 (Fast PWM)
    //WGM11 = 1, COM1A1 = 1
    //Fast PWM: TOP=ICR1, update of OCR1x=BOTTOM, TOV1 Flag Set on TOP
    
  
    unsigned int v=0;
    int indscale=0;
    float prescale[] = {1.0,8.0,64.0,256.0,1024.0};
    float period=1/frequency;
    
    while(v==0)
    {
      float curfreq=maxFreq/prescale[indscale];
      float tickperiod=1/curfreq;
      float nbtick=period/tickperiod;
     
      if(nbtick>65535)
      {
        indscale=indscale+1;
      }
      else
      {
        v=nbtick;
      }

    }
    
    int c=prescale[indscale];
    
     switch (c) {
      
         case 1: TCCR1B=0b00011001; break;
         case 8: TCCR1B=0b00011010; break;
         case 64: TCCR1B=0b00011011; break;
         case 256: TCCR1B=0b00011100; break;
         case 1024: TCCR1B=0b00011101; break;
         default: TCCR1B=0b00011000;
     }
    
    //WGM12 = 1, WGM13 = 1
    
    //three last bit of TCCR1B:    CS12   CS11   CS10
    // 0: no clock (timer stopped)  0      0      0
    // clk/1: no prescaling         0      0      1 
    // clk/8                        0      1      0
    // clk/64                       0      1      1
    // clk/256                      1      0      0
    // clk/1024                     1      0      1

    
    ICR1=v; //pulse duration = ICR1 value x time per counter tick
    
    //for 16Mhz (chip frequency)
    //Prescale	Time per counter tick
    //1	        0.0625 uS
    //8	        0.5 uS
    //64	4 uS
    //256	16 uS
    //1024	64uS
    
    OCR1A=v/2; //Output Compare Register //low state

  }
  
  
}

// code stored in the sketch: SendData.ino
	byte yMSB=0, yLSB=0, xMSB=0, xLSB=0, zeroByte=128, Checksum=0;  
 
    void SendData(int Command, unsigned int yValue,unsigned int xValue){
    

      
      /* >=================================================================< 
          y = 01010100 11010100    (x & y are 2 Byte integers)
               yMSB      yLSB      send seperately -> reciever joins them
        >=================================================================<  */
       
        yLSB=lowByte(yValue);
        yMSB=highByte(yValue);
        xLSB=lowByte(xValue);
        xMSB=highByte(xValue);        
   
      
     /* >=================================================================< 
        Only the very first Byte may be a zero, this way allows the computer 
        to know that if a Byte recieved is a zero it must be the start byte.
        If data bytes actually have a value of zero, They are given the value 
        one and the bit in the zeroByte that represents that Byte is made 
        high.  
        >=================================================================< */   
        
       zeroByte = 128;                                   // 10000000
   
       if(yLSB==0){ yLSB=1; zeroByte=zeroByte+1;}        // Make bit 1 high 
       if(yMSB==0){ yMSB=1; zeroByte=zeroByte+2;}        // make bit 2 high
       if(xLSB==0){ xLSB=1; zeroByte=zeroByte+4;}        // make bit 3 high
       if(xMSB==0){ xMSB=1; zeroByte=zeroByte+8;}        // make bit 4 high
       

     /* >=================================================================< 
        Calculate the remainder of: sum of all the Bytes divided by 255 
        >=================================================================< */
        
       Checksum = (Command + yMSB + yLSB + xMSB + xLSB + zeroByte)%255;
       
       if( Checksum !=0 ){
        Serial.write(byte(0));            // send start bit 
        Serial.write(byte(Command));      // command eg: Which Graph is this data for
        
        Serial.write(byte(yMSB));         // Y value's most significant byte  
        Serial.write(byte(yLSB));         // Y value's least significant byte   
        Serial.write(byte(xMSB));         // X value's most significant byte  
        Serial.write(byte(xLSB));         // X value's least significant byte  
        
        Serial.write(byte(zeroByte));     // Which values have a zero value
        Serial.write(byte(Checksum));     // Error Checking Byte
       }
    }  
    


       
 void PlottArray(unsigned int Cmd,float Array1[],float Array2[]){
   
      SendData(Cmd+1, 1,1);                        // Tell PC an array is about to be sent                      
      delay(1);
      for(int x=0;  x < sizeOfArray;  x++){     // Send the arrays 
        SendData(Cmd, round(Array1[x]),round(Array2[x]));
        //delay(1);
      }
      
      SendData(Cmd+2, 1,1);                        // Confirm arrrays have been sent
    }
